# Fritzing sketch greenhouse_v0.1.1 (saved by Fritzing 1.0.0rc)
breadboards: 1

parts:
  Arduino_NANO = Arduino Nano (Rev3.0)
  Moistur_ANA = Soil Moisture Sensor
  DHT11_DIG = Humidity and Temperature Sensor DHT11
  PHOTO_R = PHOTOCELL [package=photocell]
  R2 = Temperature Sensor (Thermistor) [thermistor_type=NTC package=THT]  # not connected
  S1 = Pushbutton [package="[THT]"]
  LED1 = LED - 3mm [color="Orange (612nm)" current=0.030A package="3 mm [THT]"]  # not connected
  J1 = screw terminal, 2 pins
  V1 = DC Power [voltage=12V part_number=alimentatore]  # not connected
  R3 = Resistor [tolerance=±5% power=0.25W resistance=4.7k package=THT]
  S2 = Pushbutton [package="[THT]"]  # not connected

nets:
  GND: Arduino_NANO.GND, Moistur_ANA.GND, DHT11_DIG.GND_1, S1.Pin_2, J1.pin2, R3.Pin_1
  N1: Arduino_NANO.D8, S1.Pin_4
  N2: Arduino_NANO.VIN, J1.pin1
  VCC: Arduino_NANO.5V, Moistur_ANA.VCC, DHT11_DIG.Vcc, PHOTO_R.P$1
  N3: Arduino_NANO.A0, PHOTO_R.P$2, R3.Pin_0

custom parts:
  Humidity and Temperature Sensor DHT11: Digital relative humidity & temperature sensor DHT11
