# Fritzing sketch greenhouse_v1.0.1 (saved by Fritzing 1.0.0rc)
circuit board: 10cm x 6cm
breadboards: 1

parts:
  DHT11_DIG = Humidity and Temperature Sensor DHT11  # not connected
  PWR = LED - 3mm [color="Green (565nm)" current=0.030A package="3 mm [THT]"]
  YL-69 = FC-28 Soil Hygrometer Module - Probe  # not connected
  DS1 = DS18B20 1-Wire Temperature Sensor [part_number=DS18B20]
  Q2 = Basic FET N-Channel [package="TO220 [THT]"]  # not connected
  PUMP = LED - 3mm [color="Green (565nm)" current=0.030A package="3 mm [THT]"]
  HEAT = LED - 3mm [color="Green (565nm)" current=0.030A package="3 mm [THT]"]
  R6 = Resistor [tolerance=±5% power=0.25W resistance=220 package=THT]
  R7 = Resistor [tolerance=±5% power=0.25W resistance=220 package=THT]
  R8 = Resistor [tolerance=±5% power=0.25W resistance=220 package=THT]
  R9 = Resistor [tolerance=±5% power=0.25W resistance=4.7k package=THT]
  PHOTO_R1 = PHOTOCELL [package=photocell]
  pot_T = Rotary Potentiometer (Large) [maximum_resistance=5kΩ knob_status=50% power=0.5W package=THT]
  pot_L = Rotary Potentiometer (Large) [maximum_resistance=5kΩ knob_status=50% power=0.5W package=THT]
  R10 = Resistor [tolerance=±5% power=0.25W resistance=4.7k package=THT]
  R11 = Resistor [tolerance=±5% power=0.25W resistance=4.7k package=THT]
  BTN_LAMP = Pushbutton [package="[THT]"]
  BTN_WLK = Pushbutton [package="[THT]"]
  BTN_DSPL = Pushbutton [package="[THT]"]
  LCD = screw terminal, 4 pins
  PROXY_TANK = screw terminal, 2 pins
  Q3 = NPN-Transistor [package="TO92 [THT]"]
  pot_H = Rotary Potentiometer (Large) [maximum_resistance=5kΩ knob_status=50% power=0.5W package=THT]
  DHT11 = screw terminal, 3 pins
  RELAYS = screw terminal, 3 pins
  DS18B20 = screw terminal, 3 pins
  YL-70 = FC-28 Soil Hygrometer Module
  PHOTO_R = screw terminal, 2 pins
  Pad1 = Pad [width=5 height=5 connect=center]  # not connected
  Arduino_NANO1 = Arduino Nano (Rev3.0)
  DZ9v1 = DIODE-ZENER [package=diode-zener]
  R12 = Resistor [tolerance=±5% power=3W resistance=220 package=THT]
  LM7805-1 = Voltage Regulator - 5V [package="TO220 [THT]"]
  C1 = Electrolytic Capacitor [capacitance=100nF voltage=16V package="100 mil [THT, electrolytic]"]
  C2 = Electrolytic Capacitor [capacitance=330nF voltage=16V package="100 mil [THT, electrolytic]"]
  Power_plug1 = Power plug

nets:
  GND: PWR.cathode, DS1.GND, PUMP.cathode, HEAT.cathode, R9.Pin_1, pot_T.leg1, pot_L.leg1, BTN_LAMP.Pin_1, BTN_LAMP.Pin_2, BTN_WLK.Pin_1, BTN_WLK.Pin_2, BTN_DSPL.Pin_2, LCD.pin4, PROXY_TANK.pin2, Q3.E, pot_H.leg1, DHT11.pin3, DS18B20.pin3, Arduino_NANO1.GND, DZ9v1.A, C1.-, Power_plug1.GND
  N1: PWR.anode, R6.Pin_1
  5V: DS1.VDD, PHOTO_R1.P$1, pot_T.leg2, pot_L.leg2, R11.Pin_0, LCD.pin1, pot_H.leg2, DHT11.pin1, DS18B20.pin1, YL-70.VCC, PHOTO_R.pin1, LM7805-1.output_voltage, C1.+
  N2: PUMP.anode, R7.Pin_1
  N3: HEAT.anode, R8.Pin_1
  N4: R6.Pin_0, Arduino_NANO1.D13/SCK
  N5: R7.Pin_0, Arduino_NANO1.D11/MOSI
  N6: R8.Pin_0, Arduino_NANO1.D12/MISO
  N7: R9.Pin_0, PHOTO_R1.P$2, PHOTO_R.pin2, Arduino_NANO1.A0
  N8: pot_T.wiper, Arduino_NANO1.A1
  N9: pot_L.wiper, Arduino_NANO1.A3
  N10: R10.Pin_0, Arduino_NANO1.A7
  N11: R10.Pin_1, Q3.B
  N12: R11.Pin_1, DS18B20.pin2, Arduino_NANO1.D7
  N13: BTN_LAMP.Pin_3, BTN_LAMP.Pin_4, Arduino_NANO1.D5
  N14: BTN_WLK.Pin_3, BTN_WLK.Pin_4, Arduino_NANO1.D4
  N15: BTN_DSPL.Pin_3, BTN_DSPL.Pin_4, Arduino_NANO1.D3
  N16: LCD.pin2, Arduino_NANO1.A4
  N17: LCD.pin3, Arduino_NANO1.A5
  N18: PROXY_TANK.pin1, Arduino_NANO1.D2
  N19: Q3.C, YL-70.GND
  N20: pot_H.wiper, Arduino_NANO1.A2
  N21: DHT11.pin2, Arduino_NANO1.D6
  N22: RELAYS.pin1, Arduino_NANO1.D10
  N23: RELAYS.pin2, Arduino_NANO1.D9
  N24: RELAYS.pin3, Arduino_NANO1.D8
  N25: YL-70.AO, Arduino_NANO1.A6
  +9v1: Arduino_NANO1.VIN, DZ9v1.C, R12.Pin_1
  N26: R12.Pin_0, LM7805-1.input_voltage, C2.+, Power_plug1.VCC
  N27: LM7805-1.GND, C2.-

custom parts:
  Humidity and Temperature Sensor DHT11: Digital relative humidity & temperature sensor DHT11
  FC-28 Soil Hygrometer Module - Probe: The FC-28 is a soil hygrometer module that uses the Texas Instruments LM393 comparator chip to provide an analog measurement of soil humidity.
  FC-28 Soil Hygrometer Module: The FC-28 is a soil hygrometer module that uses the Texas Instruments LM393 comparator chip to provide an analog measurement of soil humidity. The digital output is high when soil moisture is over a certain threshold, as determined by adjusting the potentiometer.
